# Fritzing sketch schema (saved by Fritzing 0.9.3b)
breadboards: 1

parts:
  Componente1 = Arduino Uno (Rev3) - ICSP
  J1 = Piezo Speaker
  J2 = Piezo Speaker
  J3 = Piezo Speaker
  J4 = Piezo Speaker
  J5 = Piezo Speaker
  J6 = Piezo Speaker
  LED1 = smd LED [color="Red (633nm)" package="0603 [SMD]"]
  LED2 = smd LED [color="Red (633nm)" package="0603 [SMD]"]
  LED3 = smd LED [color="Red (633nm)" package="0603 [SMD]"]
  LED4 = smd LED [color="Red (633nm)" package="0603 [SMD]"]
  LED5 = smd LED [color="Red (633nm)" package="0603 [SMD]"]
  LED6 = smd LED [color="Red (633nm)" package="0603 [SMD]"]

nets:
  N1: Componente1.GND, J1.pin1, J2.pin1, J3.pin1, J4.pin1, J5.pin1, J6.pin1, LED1.cathode, LED2.cathode, LED3.cathode, LED4.cathode, LED5.cathode, LED6.cathode
  N2: Componente1.D9_PWM, J3.pin2, LED3.anode
  N3: Componente1.D10_PWM/SS, J2.pin2, LED2.anode
  N4: Componente1.D11_PWM/MOSI, J1.pin2, LED1.anode
  N5: Componente1.D3_PWM, J6.pin2, LED6.anode
  N6: Componente1.D5_PWM, J5.pin2, LED5.anode
  N7: Componente1.D6_PWM, J4.pin2, LED4.anode
